# Fritzing sketch temp_sensor (saved by Fritzing 0.9.4)
breadboards: 1

parts:
  Temp_sensor_1 = DS18B20 1-Wire Temperature Sensor [part_number=DS18B20]
  Temp_sensor_2 = DS18B20 1-Wire Temperature Sensor [part_number=DS18B20]
  Temp_sensor_3 = DS18B20 1-Wire Temperature Sensor [part_number=DS18B20]
  Pi_Zero = Raspberry Pi Zero
  R1 = Resistor [tolerance=±5% resistance=4.7k package="0402 [SMD]"]
  E-paper_display = Adafruit 1.54" Tri-Color eInk / ePaper Display with SRAM
  Led_strip = WS2812 RGB LED strip
  S1 = Toggle Switch [package=THT]

nets:
  GND: Temp_sensor_1.GND, Temp_sensor_2.GND, Temp_sensor_3.GND, Pi_Zero.pin_9, Pi_Zero.pin_14, Pi_Zero.pin_39, E-paper_display.GND, Led_strip.GND
  N1: Temp_sensor_1.DQ, Temp_sensor_2.DQ, Temp_sensor_3.DQ, Pi_Zero.pin_7, R1.Pin_0
  VDD: Temp_sensor_1.VDD, Temp_sensor_2.VDD, Temp_sensor_3.VDD, Pi_Zero.pin_1, Pi_Zero.pin_17, R1.Pin_1
  N2: Pi_Zero.pin_2, Pi_Zero.pin_4, E-paper_display.VIN, S1.COM
  N3: Pi_Zero.pin_11, E-paper_display.BUSY
  N4: Pi_Zero.pin_12, Led_strip.DIN
  N5: Pi_Zero.pin_13, E-paper_display.RESET
  N6: Pi_Zero.pin_15, E-paper_display.DC
  N7: Pi_Zero.pin_19, E-paper_display.MOSI
  N8: Pi_Zero.pin_23, E-paper_display.SCLK
  N9: Pi_Zero.pin_24, E-paper_display.DISPCS
  N10: Led_strip.VCC, S1.L2

custom parts:
  Adafruit 1.54" Tri-Color eInk / ePaper Display with SRAM: This small 1.54" tri-color display has 152x152 black and red ink pixels and a white-ish background. Using our Arduino library, you can create a 'frame buffer' with what pixels you want to have activated and then write that out to the display. We tossed a small SRAM chip on the back. This chip shares the SPI port the eInk display uses, so you only need one extra pin. And, no more frame-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
  WS2812 RGB LED strip: WS2812 strip
